# Fritzing sketch full breadboard v2 (saved by Fritzing 0.9.3b)
breadboards: 2

parts:
  S1 = Pushbutton [package="[THT]"]
  S2 = Pushbutton [package="[THT]"]
  S3 = Pushbutton [package="[THT]"]
  S4 = Pushbutton [package="[THT]"]
  S5 = Pushbutton [package="[THT]"]
  S6 = Pushbutton [package="[THT]"]
  S7 = Pushbutton [package="[THT]"]
  S8 = Pushbutton [package="[THT]"]
  U2 = POT [package=pot_alpha_rv16af-20]
  U3 = POT [package=pot_alpha_rv16af-20]
  IC1 = IC, DIP package, 16 pins [chip_label=CD4051BE]
  IC2 = IC, DIP package, 16 pins [chip_label=CD4051BE]
  IC3 = IC, DIP package, 16 pins [chip_label=CD4051BE]
  IC4 = IC, DIP package, 16 pins [chip_label=CD4051BE]
  IC5 = IC, DIP package, 16 pins [chip_label=CD4051BE]
  U6 = MIDI_CONN_FEMALE_SUPPORT [package=din_5_female_support]  # not connected
  Teensy_3_1 = Teensy 3.1
  LED1 = LED - 5mm [color="Red (633nm)" package="5 mm [THT]"]
  IC6 = IC, DIP package, 8 pins [chip_label=6N139]
  R1 = Resistor [tolerance=±5% resistance=220 package=THT]

nets:
  N1: S1.Pin_1, S1.Pin_2, S2.Pin_1, S2.Pin_2, S3.Pin_1, S3.Pin_2, S4.Pin_1, S4.Pin_2, S5.Pin_1, S5.Pin_2, S6.Pin_1, S6.Pin_2, S7.Pin_1, S7.Pin_2, S8.Pin_1, S8.Pin_2, U2.E, U3.E, IC1.pin6, IC1.pin7, IC1.pin8, IC2.pin6, IC2.pin7, IC2.pin8, IC3.pin6, IC3.pin7, IC3.pin8, IC4.pin6, IC4.pin7, IC4.pin8, IC5.pin6, IC5.pin7, IC5.pin8, Teensy_3_1.GND
  N2: S1.Pin_3, S1.Pin_4, IC1.pin13
  N3: S2.Pin_3, S2.Pin_4, IC1.pin14
  N4: S3.Pin_3, S3.Pin_4, IC1.pin15
  N5: S4.Pin_3, S4.Pin_4, IC1.pin12
  N6: S5.Pin_3, S5.Pin_4, IC1.pin1
  N7: S6.Pin_3, S6.Pin_4, IC1.pin5
  N8: S7.Pin_3, S7.Pin_4, IC1.pin2
  N9: S8.Pin_3, S8.Pin_4, IC1.pin4
  N10: U2.A, U3.A, IC1.pin16, IC2.pin16, IC3.pin16, IC4.pin16, IC5.pin16, Teensy_3_1.3V3
  N11: IC1.pin9, IC3.pin9, IC4.pin9, Teensy_3_1.D7
  N12: IC1.pin10, IC3.pin10, IC4.pin10, Teensy_3_1.D6
  N13: IC1.pin11, IC3.pin11, IC4.pin11, Teensy_3_1.D5
  N14: IC2.pin1, IC3.pin1
  N15: IC2.pin2, IC3.pin2
  N16: IC2.pin4, IC3.pin4
  N17: IC2.pin5, IC3.pin5
  N18: IC2.pin9, IC5.pin9, Teensy_3_1.D4
  N19: IC2.pin10, IC5.pin10, Teensy_3_1.D3
  N20: IC2.pin11, IC5.pin11, Teensy_3_1.D2
  N21: IC2.pin12, IC3.pin12
  N22: IC2.pin13, IC3.pin13
  N23: IC2.pin14, IC3.pin14
  N24: IC2.pin15, IC3.pin15
  N25: IC4.pin1, IC5.pin1
  N26: IC4.pin2, IC5.pin2
  N27: IC4.pin4, IC5.pin4
  N28: IC4.pin5, IC5.pin5
  N29: IC4.pin12, IC5.pin12
  N30: IC4.pin13, IC5.pin13
  N31: IC4.pin14, IC5.pin14
  N32: IC4.pin15, IC5.pin15
  N33: Teensy_3_1.D0, IC6.pin6
  N34: Teensy_3_1.A6/D20, R1.Pin_0
  N35: Teensy_3_1.Vin, IC6.pin8
  N36: LED1.anode, R1.Pin_1
