# Fritzing sketch full breadboard (saved by Fritzing 0.9.3b)
breadboards: 3

parts:
  S1 = Pushbutton [package="[THT]"]
  S2 = Pushbutton [package="[THT]"]
  S3 = Pushbutton [package="[THT]"]
  S4 = Pushbutton [package="[THT]"]
  S5 = Pushbutton [package="[THT]"]
  S6 = Pushbutton [package="[THT]"]
  S7 = Pushbutton [package="[THT]"]
  S8 = Pushbutton [package="[THT]"]
  U1 = POT [package=pot_alpha_rv16af-20]
  U2 = POT [package=pot_alpha_rv16af-20]
  U3 = POT [package=pot_alpha_rv16af-20]
  U4 = POT [package=pot_alpha_rv16af-20]
  U5 = POT [package=pot_alpha_rv16af-20]
  IC1 = IC, DIP package, 16 pins [chip_label=CD4051BE]
  IC2 = IC, DIP package, 16 pins [chip_label=CD4051BE]
  IC3 = IC, DIP package, 16 pins [chip_label=CD4051BE]
  IC4 = IC, DIP package, 16 pins [chip_label=CD4051BE]
  IC5 = IC, DIP package, 16 pins [chip_label=CD4051BE]
  U6 = MIDI_CONN_FEMALE_SUPPORT [package=din_5_female_support]  # not connected
  Teensy_3_1 = Teensy 3.1
  LED1 = LED - 5mm [color="Red (633nm)" package="5 mm [THT]"]  # not connected
  IC6 = IC, DIP package, 8 pins [chip_label=6N139]

nets:
  N1: S1.Pin_1, S1.Pin_2, S2.Pin_1, S2.Pin_2, S3.Pin_1, S3.Pin_2, S4.Pin_1, S4.Pin_2, S5.Pin_1, S5.Pin_2, S6.Pin_1, S6.Pin_2, S7.Pin_1, S7.Pin_2, S8.Pin_1, S8.Pin_2, U1.E, U2.E, U3.E, U4.E, U5.E, IC1.pin6, IC1.pin7, IC1.pin8, IC2.pin6, IC2.pin7, IC2.pin8, IC3.pin6, IC3.pin7, IC3.pin8, IC4.pin6, IC4.pin7, IC4.pin8, IC5.pin6, IC5.pin7, IC5.pin8, Teensy_3_1.GND, IC6.pin5
  N2: S1.Pin_3, S1.Pin_4
  N3: S2.Pin_3, S2.Pin_4
  N4: S3.Pin_3, S3.Pin_4
  N5: S4.Pin_3, S4.Pin_4
  N6: S5.Pin_3, S5.Pin_4
  N7: S6.Pin_3, S6.Pin_4
  N8: S7.Pin_3, S7.Pin_4
  N9: S8.Pin_3, S8.Pin_4
