# Fritzing sketch part1 breadboard (saved by Fritzing 0.9.3b)
breadboards: 1

parts:
  IC2 = IC, DIP package, 16 pins [chip_label=CD4051BE]
  IC3 = IC, DIP package, 16 pins [chip_label=CD4051BE]
  Teensy_3_1 = Teensy 3.1
  LED1 = LED - 5mm [color="Red (633nm)" package="5 mm [THT]"]
  R1 = Resistor [tolerance=±5% resistance=220 package=THT]

nets:
  N1: IC2.pin1, IC3.pin1
  N2: IC2.pin2, IC3.pin2
  N3: IC2.pin4, IC3.pin4
  N4: IC2.pin5, IC3.pin5
  N5: IC2.pin6, IC2.pin7, IC2.pin8, IC3.pin6, IC3.pin7, IC3.pin8, Teensy_3_1.GND
  N6: IC2.pin9, Teensy_3_1.D4
  N7: IC2.pin10, Teensy_3_1.D3
  N8: IC2.pin11, Teensy_3_1.D2
  N9: IC2.pin12, IC3.pin12
  N10: IC2.pin13, IC3.pin13
  N11: IC2.pin14, IC3.pin14
  N12: IC2.pin15, IC3.pin15
  N13: IC2.pin16, IC3.pin16, Teensy_3_1.3V3
  N14: IC3.pin9, Teensy_3_1.D7
  N15: IC3.pin10, Teensy_3_1.D6
  N16: IC3.pin11, Teensy_3_1.D5
  N17: LED1.anode, R1.Pin_0
